// Logisim project SingleCycleCPU.circ as structural Verilog: 1 circuit, main circuit Datapath
module Datapath (
  input  Reset,
  input  Clear_Data_Mem,
  input  Clear_Instr_Mem
);

  wire ALU_zero, Branch_Control_control, Clock_out, Controls_alusrc, Controls_conditional_branch,
       Controls_memread, Controls_memtoreg, Controls_memwrite, Controls_reg2loc, Controls_regwrite,
       Controls_unconditional_branch;
  wire [1:0] data_mem_interface_1_mem_control;
  wire [3:0] alucontrol_1_operation;
  wire [4:0] instructiondecode_1_rd_rt, instructiondecode_1_rm, instructiondecode_1_rn, multiplexer_1_out;
  wire [7:0] data_mem_interface_1_address_to_mem, inst_mem_interface_1_to_inst_mem;
  wire [10:0] instructiondecode_1_opcode, instructiondecode_1_opcodealu;
  wire [31:0] adder_1_out, ALU_result, Branch_Address_branchaddress, data_mem_interface_1_data_from_mem,
       data_mem_interface_1_data_from_memory, inst_mem_interface_1_instruction,
       instructiondecode_1_sign_ext_0_31, multiplexer_2_out, multiplexer_3_out, multiplexer_4_out, PC_q,
       ram_1_data, Register_file_readdata1, Register_file_readdata2, signextend_1_out_2;

  Register #(.width(32)) PC (.D(multiplexer_3_out), .Q(PC_q), .clk(Clock_out), .clr(Reset));  // open: en
  Clock Clock (.out(Clock_out));
  Inst_Mem_Interface inst_mem_interface_1 (
    .Instruction_Address(PC_q), .To_Inst_Mem(inst_mem_interface_1_to_inst_mem),
    .Mem_To_Interface(ram_1_data), .Instruction(inst_mem_interface_1_instruction));
  Adder #(.width(32)) adder_1 (.a(32'h4), .b(PC_q), .out(adder_1_out));  // open: cin, cout
  InstructionDecode instructiondecode_1 (
    .Instruction(inst_mem_interface_1_instruction), .opcode(instructiondecode_1_opcode),
    .rn(instructiondecode_1_rn), .rm(instructiondecode_1_rm), .rd_rt(instructiondecode_1_rd_rt),
    .Sign_Ext_0_31(instructiondecode_1_sign_ext_0_31), .opcodeALU(instructiondecode_1_opcodealu));  // open: shamt
  RAM #(.dataWidth(32)) ram_1 (
    .addr(inst_mem_interface_1_to_inst_mem), .data(ram_1_data), .sel(1'b1), .clk(1'b0), .ld(1'b1),
    .clr(Clear_Instr_Mem));
  Control Controls (
    .op(instructiondecode_1_opcode), .Unconditional_Branch(Controls_unconditional_branch),
    .Conditional_Branch(Controls_conditional_branch), .MemToReg(Controls_memtoreg),
    .MemRead(Controls_memread), .MemWrite(Controls_memwrite), .ALUsrc(Controls_alusrc),
    .RegWrite(Controls_regwrite), .Reg2Loc(Controls_reg2loc));
  Multiplexer #(.width(5), .enable("false")) multiplexer_1 (
    .in0(instructiondecode_1_rm), .in1(instructiondecode_1_rd_rt), .out(multiplexer_1_out),
    .sel(Controls_reg2loc));
  SignExtend signextend_1 (._0_31(instructiondecode_1_sign_ext_0_31), .out_2(signextend_1_out_2));
  Registers Register_file (
    .ReadRegister1(instructiondecode_1_rn), .ReadRegister2(multiplexer_1_out),
    .WriteRegister(instructiondecode_1_rd_rt), .WriteData(multiplexer_4_out), .Write(Controls_regwrite),
    .Clock(Clock_out), .Clear(Reset), .ReadData1(Register_file_readdata1), .ReadData2(Register_file_readdata2));
  ALUcontrol alucontrol_1 (.opcode(instructiondecode_1_opcodealu), .Operation(alucontrol_1_operation));
  BranchAddress Branch_Address (.PC(PC_q), .Address(signextend_1_out_2), .BranchAddress(Branch_Address_branchaddress));
  Multiplexer #(.width(32), .enable("false")) multiplexer_2 (
    .in0(Register_file_readdata2), .in1(signextend_1_out_2), .out(multiplexer_2_out), .sel(Controls_alusrc));
  ALU ALU (
    .A(Register_file_readdata1), .B(multiplexer_2_out), .Operation(alucontrol_1_operation), .Zero(ALU_zero),
    .Result(ALU_result));  // open: Sign, Overflow, Carry_Out
  Multiplexer #(.width(32), .enable("false")) multiplexer_3 (
    .in0(adder_1_out), .in1(Branch_Address_branchaddress), .out(multiplexer_3_out),
    .sel(Branch_Control_control));
  BranchControl Branch_Control (
    .UnconditionalBranch(Controls_unconditional_branch),
    .ConditionalBranch__CBZ(Controls_conditional_branch), .Zero(ALU_zero), .control(Branch_Control_control));
  Data_Mem_Interface data_mem_interface_1 (
    .Data_Address(ALU_result), .Data_to_Memory(Register_file_readdata2), .MemWrite(Controls_memwrite),
    .MemRead(Controls_memread), .Clock___Rising_Edge(Clock_out),
    .Address_To_Mem(data_mem_interface_1_address_to_mem), .Mem_Control(data_mem_interface_1_mem_control),
    .Data_To_Mem(data_mem_interface_1_data_from_mem), .Data_From_Mem(data_mem_interface_1_data_from_mem),
    .Data_from_Memory(data_mem_interface_1_data_from_memory));
  Multiplexer #(.width(32), .enable("false")) multiplexer_4 (
    .in0(ALU_result), .in1(data_mem_interface_1_data_from_memory), .out(multiplexer_4_out),
    .sel(Controls_memtoreg));
  RAM #(.dataWidth(32)) ram_2 (
    .addr(data_mem_interface_1_address_to_mem), .data(data_mem_interface_1_data_from_mem), .sel(1'b1),
    .clk(data_mem_interface_1_mem_control[0]), .ld(data_mem_interface_1_mem_control[1]), .clr(Clear_Data_Mem));

  // Notes on the sheet:
  //   F19
  //   Mia McDuffie
  //   11/03/2019
  //   Decode
  //   Sign Ext
  //   ALU Control
  //   Br Control
endmodule
